# Fritzing sketch digital out (saved by Fritzing 0.9.1b)
breadboards: 2

parts:
  module1 = scratch_n_sketch [package="DIP (Dual Inline) [THT]"]
  LED1 = LED - 3mm [color="Red (633nm)" package="3 mm [THT]"]
  R1 = Resistor [tolerance=±5% resistance=220 package="1206 [SMD]"]
  U1 = TMP36 [package=to-92-kit]

nets:
  N1: module1.pin4, LED1.cathode
  N2: module1.pin6, U1.VOUT
  N3: module1.pin7, U1.VCC
  N4: module1.pin8, R1.Pin_1, U1.GND
  N5: LED1.anode, R1.Pin_0

notes:
  TMP36
  LED
  RED
  TEMP SENSOR

custom parts:
  scratch_n_sketch: scratch n sketch module
